// Logisim project cpu.circ as structural Verilog: 3 circuits, main circuit main
module main (
  input  [31:0] in_1
);

  wire clock_1_out, comparator_1_eq, demultiplexer_2_out0, demultiplexer_2_out1, demultiplexer_2_out2;
  wire [2:0] alu_1_compare_bits;
  wire [7:0] A_q, alu_1_output, D_q, demultiplexer_1_out0, demultiplexer_1_out1, demultiplexer_1_out2,
       multiplexer_1_out, multiplexer_2_out, multiplexer_3_out, multiplexer_4_out, pc_1_out, ram_1_data,
       rom_1_data;
  wire [31:0] rom_1_data_2;

  Multiplexer #(.width(8), .enable("false")) multiplexer_1 (
    .in0(demultiplexer_1_out0), .in1(rom_1_data_2[27:20]), .out(multiplexer_1_out), .sel(rom_1_data_2[11]));
  Clock clock_1 (.out(clock_1_out));
  Multiplexer #(.select(2), .width(8), .enable("false")) multiplexer_2 (
    .in0(A_q), .in1(A_q), .in2(A_q), .in3(rom_1_data), .out(multiplexer_2_out), .sel(rom_1_data_2[4:3]));
  Register A (.D(multiplexer_1_out), .en(demultiplexer_2_out0), .Q(A_q), .clk(clock_1_out));  // open: clr
  Register D (.D(demultiplexer_1_out1), .en(demultiplexer_2_out1), .Q(D_q), .clk(clock_1_out));  // open: clr
  PC pc_1 (.load(comparator_1_eq), .\input (multiplexer_2_out), .clock(clock_1_out), .reset(1'b0), .out(pc_1_out));
  Multiplexer #(.select(2), .width(8), .enable("false")) multiplexer_3 (
    .in0(A_q), .in1(D_q), .in2(ram_1_data), .in3(rom_1_data_2[27:20]), .out(multiplexer_3_out),
    .sel(rom_1_data_2[10:9]));
  Multiplexer #(.select(2), .width(8), .enable("false")) multiplexer_4 (
    .in0(A_q), .in1(D_q), .in2(ram_1_data), .in3(rom_1_data_2[27:20]), .out(multiplexer_4_out),
    .sel(rom_1_data_2[8:7]));
  alu alu_1 (
    .input1(multiplexer_3_out), .input2(multiplexer_4_out), .control(rom_1_data_2[31:28]),
    .\output (alu_1_output), .compare_bits(alu_1_compare_bits));
  Demultiplexer #(.select(2), .width(8), .enable("false")) demultiplexer_1 (
    .out0(demultiplexer_1_out0), .out1(demultiplexer_1_out1), .out2(demultiplexer_1_out2), .in(alu_1_output),
    .sel(rom_1_data_2[6:5]));  // open: out3
  ROM #(.dataWidth(32)) rom_1 (
    .addr(pc_1_out), .data({rom_1_data_2[31:20], rom_1_data, rom_1_data_2[11:0]}), .sel(1'b1));
  Demultiplexer #(.select(2), .enable("false")) demultiplexer_2 (
    .out0(demultiplexer_2_out0), .out1(demultiplexer_2_out1), .out2(demultiplexer_2_out2), .in(1'b1),
    .sel(rom_1_data_2[6:5]));  // open: out3
  Comparator #(.width(3)) comparator_1 (
    .a(alu_1_compare_bits), .b(rom_1_data_2[2:0]), .eq(comparator_1_eq));  // open: gt, lt
  RAM #(.bus("separate")) ram_1 (
    .addr(A_q), .din(demultiplexer_1_out2), .data(ram_1_data), .str(demultiplexer_2_out2), .sel(1'b1),
    .clk(clock_1_out), .ld(1'b1));  // open: clr

  // Notes on the sheet:
  //   contents of rom_1 (hex, n*v repeats v):
  //   800 640 100800 100640 100620 800 200004c0 100800 420 200800 20000320 300800 240 200800 420 100800
  //   240 300800 420 200800 240 800 420 400800 600384
endmodule

module alu (
  input  [7:0] input1,
  input  [7:0] input2,
  input  [3:0] control,
  output [7:0] \output ,
  output [2:0] compare_bits
);

  wire [7:0] adder_1_out, and_1_out, multiplier_1_out, not_1_out, or_1_out, subtractor_1_out;

  Adder adder_1 (.a(input1), .b(input2), .out(adder_1_out));  // open: cin, cout
  Subtractor subtractor_1 (.a(input1), .b(input2), .out(subtractor_1_out));  // open: bin, bout
  Multiplier multiplier_1 (.a(input1), .b(input2), .out(multiplier_1_out));  // open: cin, cout
  assign and_1_out = input1 & input2;  // AND_Gate and_1, 8 bits wide
  assign or_1_out = input1 | input2;  // OR_Gate or_1, 8 bits wide
  assign not_1_out = ~input1;  // NOT_Gate not_1, 8 bits wide
  Comparator comparator_1 (.a(input1), .b(input2), .gt(compare_bits[0]), .eq(compare_bits[1]), .lt(compare_bits[2]));
  Multiplexer #(.select(4), .width(8), .enable("false")) multiplexer_1 (
    .in0(input1), .in1(input2), .in2(adder_1_out), .in3(subtractor_1_out), .in4(multiplier_1_out),
    .in5(and_1_out), .in6(or_1_out), .in7(not_1_out), .out(\output ), .sel(control));  // open: in8, in9, in10, in11, in12, in13, in14, in15
endmodule

module PC (
  input  load,
  input  [7:0] \input ,
  input  clock,
  input  reset,
  output [7:0] out
);

  wire not_1_out;

  not not_1 (not_1_out, load);
  Counter counter_1 (.load(load), .D(\input ), .count(not_1_out), .Q(out), .clk(clock), .clr(reset));  // open: carry
endmodule
